# Fritzing sketch Self_balance_bot_sketch (saved by Fritzing 0.9.3b)
circuit board: 8.46667cm x 5.64444cm

parts:
  U1 = ESP32S-HiLetgo [part_number=ESP32S-HiLetgo]
  Part1 = InvenSense MPU6050
  IC1 = Voltage Regulator [package=78xxl]
  V1 = DC Power [voltage=5]
  Pololu_A1 = Pololu A4988 [package=SO16]
  Pololu_A2 = Pololu A4988 [package=SO16]

nets:
  N1: U1.GPIO14, Pololu_A1.STEP
  N2: U1.GPIO12, Pololu_A1.DIR
  GND: U1.GND, Part1.GND, IC1.GND, V1.V-, Pololu_A1.GND
  VIN: U1.VIN, Part1.VCC, IC1.OUT
  N3: U1.GPIO15, Pololu_A2.STEP
  N4: U1.GPIO16, Pololu_A2.DIR
  N5: U1.GPIO21, Part1.SDA
  N6: U1.GPIO22, Part1.SCL
  N7: IC1.IN, V1.V+, Pololu_A1.VMOT, Pololu_A2.VMOT
  N8: Pololu_A1.RESET, Pololu_A1.SLEEP
  VDD: Pololu_A1.VDD, Pololu_A2.VDD
  N9: Pololu_A2.RESET, Pololu_A2.SLEEP

custom parts:
  ESP32S-HiLetgo: HiLetgo ESP-WROOM-32 ESP32 ESP-32S Development Board 2.4GHz Dual-Mode WiFi + Bluetooth Dual Cores Microcontroller The ESP32 integrated with Antenna switches, RF Balun, power amplifiers, low-noise amplifiers, filters, and management modules, and the entire solution occupies the least area of PCB. 2.4 GHz Wi-Fi plus Bluetooth dual-mode chip, with TSMC Ultra-low power consumption 40nm technology,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
